# Fritzing sketch WindSensorMKR (saved by Fritzing 0.9.8b)
circuit board: 8.78467cm x 4.55958cm

parts:
  MKRFOX1200 = Arduino MKR Fox 1200
  R9 = Resistor [tolerance=±1% resistance=10k power=0.25 package=THT]
  RJ11_MISOL = RJ11 Jack [package=rj11-6]
  SOLAR = Solar Panel [package="Renogy 50 Watts 12 Volt Monocrystalline Bendable Solar Panel"]
  R10 = Resistor [tolerance=±1% resistance=560k power=0.25 package=THT]
  R11 = Resistor [tolerance=±1% resistance=390k power=0.25 package=THT]
  TP4056 = TP4056 [chip_label=TP4056 package="DIP (Dual Inline) [THT]"]
  C6 = Film/Foil Capacitor [capacitance=100nF voltage=35V package="5mm [THT, pp]"]
  C7 = Film/Foil Capacitor [capacitance=100nF voltage=35V package="5mm [THT, pp]"]
  U1_ON-OFF = SPST Switch [package=switch-spdt_kit]
  D1 = Schottky Diode [part_number=1N5817 package="300 mil [THT]"]
  D2 = Schottky Diode [part_number=1N5817 package="300 mil [THT]"]
  +BAT- = Screw terminal - 2 pins [package=THT]

nets:
  N1: MKRFOX1200.A4, R10.Pin_0, R11.Pin_1
  pinGirAdc: MKRFOX1200.A6, R9.Pin_0, RJ11_MISOL.4, C6.-, D2.cathode
  intPinAnemo: MKRFOX1200.~4, RJ11_MISOL.5, C7.-, D1.cathode
  pinGirAlim: MKRFOX1200.~5, R9.Pin_1
  GND: MKRFOX1200.GND, RJ11_MISOL.2, RJ11_MISOL.3, SOLAR.Connector_2, R11.Pin_0, TP4056.pin2, TP4056.pin5, TP4056.pin6, C6.+, C7.+, D1.anode, D2.anode, +BAT-.pin2
  N2: MKRFOX1200.VIN, U1_ON-OFF.O
  N3: SOLAR.Connector_1, TP4056.pin1
  Vbat: R10.Pin_1, TP4056.pin4, +BAT-.pin1
  N4: TP4056.pin3, U1_ON-OFF.P

notes:
  yellow
  green
  red
  black
  WindSensorMKR1200

custom parts:
  Solar Panel: Renogy 50 Watts 12 Volt Solar Panel
  TP4056: A DIP stand-in part for whatever IC you want. With 6 pins on a 300mil dual inline package (DIP) footprint.
